// Logisim project ALU - Пилипенко.circ as structural Verilog: 3 circuits, main circuit main
module main (
  input  [15:0] in_1,
  input  in_2,
  input  nx,
  input  no,
  input  zx,
  input  ny,
  input  zy,
  input  f,
  input  [15:0] in_9,
  output out_10,
  output [15:0] out_11,
  output out_12
);

  wire alu_4_bite_1_out_12, alu_4_bite_2_out_10, alu_4_bite_2_out_12, alu_4_bite_3_out_10,
       alu_4_bite_3_out_12, alu_4_bite_4_out_10, alu_4_bite_4_out_12;

  ALU_4_bite alu_4_bite_1 (
    .\х (in_1[15:12]), .nx(nx), .zx(zx), .ny(ny), .zy(zy), .f(f), .\у (in_9[15:12]),
    .in_2(alu_4_bite_2_out_10), .out_12(alu_4_bite_1_out_12), .\по (no), .\Выход (out_11[15:12]));  // open: out_10
  ALU_4_bite alu_4_bite_2 (
    .\х (in_1[11:8]), .nx(nx), .zx(zx), .ny(ny), .zy(zy), .f(f), .\у (in_9[11:8]),
    .in_2(alu_4_bite_3_out_10), .out_10(alu_4_bite_2_out_10), .out_12(alu_4_bite_2_out_12), .\по (no),
    .\Выход (out_11[11:8]));
  ALU_4_bite alu_4_bite_3 (
    .\х (in_1[7:4]), .nx(nx), .zx(zx), .ny(ny), .zy(zy), .f(f), .\у (in_9[7:4]), .in_2(alu_4_bite_4_out_10),
    .out_10(alu_4_bite_3_out_10), .out_12(alu_4_bite_3_out_12), .\по (no), .\Выход (out_11[7:4]));
  ALU_4_bite alu_4_bite_4 (
    .\х (in_1[3:0]), .nx(nx), .zx(zx), .ny(ny), .zy(zy), .f(f), .\у (in_9[3:0]), .in_2(in_2),
    .out_10(alu_4_bite_4_out_10), .out_12(alu_4_bite_4_out_12), .\по (no), .\Выход (out_11[3:0]));
  or or_1 (out_10, alu_4_bite_4_out_12, alu_4_bite_3_out_12, alu_4_bite_2_out_12, alu_4_bite_1_out_12);

  assign out_12 = out_11[15];

  // Notes on the sheet:
  //   x
  //   y
  //   Вход переноса
  //   Вывод
endmodule

module ALU (
  input  in_1,
  input  in_2,
  input  in_3,
  input  in_4,
  input  in_5,
  input  in_6,
  input  in_7,
  input  in_8,
  input  in_9,
  output out_10,
  output out_11
);

  wire and_1_out, and_2_out, and_3_out, and_4_out, and_5_out, and_6_out, and_7_out, not_1_out, not_2_out,
       not_3_out, or_2_out, xor_1_out, xor_2_out, xor_3_out, xor_4_out;

  not not_1 (not_1_out, in_5);
  not not_2 (not_2_out, in_8);
  and and_1 (and_1_out, in_4, not_1_out);
  and and_2 (and_2_out, in_7, not_2_out);
  not not_3 (not_3_out, in_9);
  xor xor_1 (xor_1_out, in_3, and_1_out);
  xor xor_2 (xor_2_out, in_6, and_2_out);
  and and_3 (and_3_out, xor_1_out, xor_2_out);
  and and_4 (and_4_out, and_3_out, not_3_out);
  and and_5 (and_5_out, in_9, xor_1_out, xor_2_out);
  xor xor_3 (xor_3_out, xor_2_out, xor_1_out);
  or or_1 (out_11, and_5_out, and_6_out);
  and and_6 (and_6_out, in_9, xor_3_out, in_1);
  xor xor_4 (xor_4_out, in_1, xor_3_out);
  and and_7 (and_7_out, xor_4_out, in_9);
  or or_2 (or_2_out, and_4_out, and_7_out);
  xor xor_5 (out_10, in_2, or_2_out);
endmodule

module ALU_4_bite (
  input  [3:0] \х ,
  input  in_2,
  input  nx,
  input  \по ,
  input  zx,
  input  ny,
  input  zy,
  input  f,
  input  [3:0] \у ,
  output out_10,
  output [3:0] \Выход ,
  output out_12
);

  wire alu_2_out_11, alu_3_out_11, alu_4_out_11;

  ALU alu_1 (
    .in_3(nx), .in_4(\х [3]), .in_5(zx), .in_6(ny), .in_7(\у [3]), .in_8(zy), .in_9(f), .in_1(alu_2_out_11),
    .in_2(\по ), .out_11(out_10), .out_10(\Выход [3]));
  ALU alu_2 (
    .in_3(nx), .in_4(\х [2]), .in_5(zx), .in_6(ny), .in_7(\у [2]), .in_8(zy), .in_9(f), .in_1(alu_3_out_11),
    .in_2(\по ), .out_11(alu_2_out_11), .out_10(\Выход [2]));
  ALU alu_3 (
    .in_3(nx), .in_4(\х [1]), .in_5(zx), .in_6(ny), .in_7(\у [1]), .in_8(zy), .in_9(f), .in_1(alu_4_out_11),
    .in_2(\по ), .out_11(alu_3_out_11), .out_10(\Выход [1]));
  or or_1 (out_12, \Выход [3], \Выход [2], \Выход [1], \Выход [0]);
  ALU alu_4 (
    .in_3(nx), .in_4(\х [0]), .in_5(zx), .in_6(ny), .in_7(\у [0]), .in_8(zy), .in_9(f), .in_1(in_2),
    .in_2(\по ), .out_11(alu_4_out_11), .out_10(\Выход [0]));

  // Notes on the sheet:
  //   Выход переноса
  //   Вход переноса
endmodule
