// Logisim project Регистры.circ as structural Verilog: 4 circuits, main circuit main
module main (
  input  [3:0] \Ввод ,
  input  \Записать ,
  input  \Очистить ,
  output [3:0] \Вывод 
);

  D_Flip_Flop d_ff_1 (.clk(\Записать ), .D(\Ввод [3]), .Q(\Вывод [3]), .reset(\Очистить ));  // open: Qn, preset, en
  D_Flip_Flop d_ff_2 (.clk(\Записать ), .D(\Ввод [2]), .Q(\Вывод [2]), .reset(\Очистить ));  // open: Qn, preset, en
  D_Flip_Flop d_ff_3 (.clk(\Записать ), .D(\Ввод [1]), .Q(\Вывод [1]), .reset(\Очистить ));  // open: Qn, preset, en
  D_Flip_Flop d_ff_4 (.clk(\Записать ), .D(\Ввод [0]), .Q(\Вывод [0]), .reset(\Очистить ));  // open: Qn, preset, en
endmodule

module \сдвиговый_регистр  (
  input  in_1,
  input  in_2,
  input  in_3
);

  wire d_ff_1_q, d_ff_2_q, d_ff_3_q, d_ff_4_q;

  D_Flip_Flop d_ff_1 (.clk(in_1), .D(in_2), .Q(d_ff_1_q), .reset(in_3));  // open: Qn, preset, en
  LED led_1 (.in(d_ff_1_q));
  D_Flip_Flop d_ff_2 (.clk(in_1), .D(d_ff_1_q), .Q(d_ff_2_q), .reset(in_3));  // open: Qn, preset, en
  LED led_2 (.in(d_ff_2_q));
  D_Flip_Flop d_ff_3 (.clk(in_1), .D(d_ff_2_q), .Q(d_ff_3_q), .reset(in_3));  // open: Qn, preset, en
  LED led_3 (.in(d_ff_3_q));
  D_Flip_Flop d_ff_4 (.clk(in_1), .D(d_ff_3_q), .Q(d_ff_4_q), .reset(in_3));  // open: Qn, preset, en
  LED led_4 (.in(d_ff_4_q));
endmodule

module \счетный_регистр  (
  input  in_1,
  input  in_2,
  input  in_3
);

  wire [3:0] t_ff_1_q;

  T_Flip_Flop t_ff_1 (.clk(in_1), .T(in_2), .Q(t_ff_1_q[0]), .reset(in_3));  // open: Qn, preset, en
  T_Flip_Flop t_ff_2 (.clk(in_1), .T(t_ff_1_q[0]), .Q(t_ff_1_q[1]), .reset(in_3));  // open: Qn, preset, en
  T_Flip_Flop t_ff_3 (.clk(in_1), .T(t_ff_1_q[1]), .Q(t_ff_1_q[2]), .reset(in_3));  // open: Qn, preset, en
  T_Flip_Flop t_ff_4 (.clk(in_1), .T(t_ff_1_q[2]), .Q(t_ff_1_q[3]), .reset(in_3));  // open: Qn, preset, en
  Hex_Digit_Display hex_digit_display_1 (.value(t_ff_1_q));  // open: dp
endmodule

module \Счетный_регистр  (
  input  in_1,
  input  in_2,
  input  in_3
);

  wire [3:0] t_ff_1_q;

  T_Flip_Flop t_ff_1 (.clk(in_1), .T(in_2), .Q(t_ff_1_q[0]), .reset(in_3));  // open: Qn, preset, en
  T_Flip_Flop t_ff_2 (.clk(in_1), .T(t_ff_1_q[0]), .Q(t_ff_1_q[1]), .reset(in_3));  // open: Qn, preset, en
  T_Flip_Flop t_ff_3 (.clk(in_1), .T(t_ff_1_q[1]), .Q(t_ff_1_q[2]), .reset(in_3));  // open: Qn, preset, en
  T_Flip_Flop t_ff_4 (.clk(in_1), .T(t_ff_1_q[2]), .Q(t_ff_1_q[3]), .reset(in_3));  // open: Qn, preset, en
  Hex_Digit_Display hex_digit_display_1 (.value(t_ff_1_q));  // open: dp
endmodule
