// Logisim project Система памяти.circ as structural Verilog: 5 circuits, main circuit main
module main (
  input  \ввод_данных ,
  input  \вход ,
  input  \такт__имп ,
  output \выход 
);

  wire and_1_out, and_2_out, not_1_out, or_1_out;

  not not_1 (not_1_out, \ввод_данных );
  and and_1 (and_1_out, \ввод_данных , \вход );
  and and_2 (and_2_out, not_1_out, \выход );
  or or_1 (or_1_out, and_1_out, and_2_out);
  D_Flip_Flop d_ff_1 (.clk(\такт__имп ), .D(or_1_out), .Q(\выход ));  // open: Qn, preset, en, reset
endmodule

module \Ячейка_памяти_D_триггер  (
  input  \ввод_данных ,
  input  \вход ,
  input  \такт__имп ,
  output \выход 
);

  wire and_1_out, and_2_out, not_1_out, or_1_out;

  not not_1 (not_1_out, \ввод_данных );
  and and_1 (and_1_out, \ввод_данных , \вход );
  and and_2 (and_2_out, not_1_out, \выход );
  or or_1 (or_1_out, and_1_out, and_2_out);
  D_Flip_Flop d_ff_1 (.clk(\такт__имп ), .D(or_1_out), .Q(\выход ));  // open: Qn, preset, en, reset
endmodule

module \Четырехразрядный_регистр  (
  input  [3:0] in_1,
  input  in_2,
  input  in_3,
  output [3:0] out_4
);

  \Ячейка_памяти_D_триггер  \u_ячейка_памяти_d_триггер_1  (
    .\вход (in_1[3]), .\ввод_данных (in_2), .\такт__имп (in_3), .\выход (out_4[3]));
  \Ячейка_памяти_D_триггер  \u_ячейка_памяти_d_триггер_2  (
    .\вход (in_1[2]), .\ввод_данных (in_2), .\такт__имп (in_3), .\выход (out_4[2]));
  \Ячейка_памяти_D_триггер  \u_ячейка_памяти_d_триггер_3  (
    .\вход (in_1[1]), .\ввод_данных (in_2), .\такт__имп (in_3), .\выход (out_4[1]));
  \Ячейка_памяти_D_триггер  \u_ячейка_памяти_d_триггер_4  (
    .\вход (in_1[0]), .\ввод_данных (in_2), .\такт__имп (in_3), .\выход (out_4[0]));
endmodule

module \шестнадцатиразрядный_регистр  (
  input  [15:0] in_1,
  input  in_2,
  input  in_3,
  output [15:0] out_4
);

  \Четырехразрядный_регистр  \u_четырехразрядный_регистр_1  (
    .in_1(in_1[15:12]), .in_2(in_2), .in_3(in_3), .out_4(out_4[15:12]));
  \Четырехразрядный_регистр  \u_четырехразрядный_регистр_2  (
    .in_1(in_1[11:8]), .in_2(in_2), .in_3(in_3), .out_4(out_4[11:8]));
  \Четырехразрядный_регистр  \u_четырехразрядный_регистр_3  (
    .in_1(in_1[7:4]), .in_2(in_2), .in_3(in_3), .out_4(out_4[7:4]));
  \Четырехразрядный_регистр  \u_четырехразрядный_регистр_4  (
    .in_1(in_1[3:0]), .in_2(in_2), .in_3(in_3), .out_4(out_4[3:0]));
endmodule

module \Оперативное_запоминающее_устройство  (
  input  in_1,
  input  [15:0] in_2,
  input  [2:0] in_3,
  input  in_4,
  output [15:0] out_5
);

  wire demultiplexer_1_out0, demultiplexer_1_out1, demultiplexer_1_out2, demultiplexer_1_out3,
       demultiplexer_1_out4, demultiplexer_1_out5, demultiplexer_1_out6, demultiplexer_1_out7;
  wire [15:0] \шестнадцатиразрядный_регистр_1_out_4 , \шестнадцатиразрядный_регистр_2_out_4 ,
       \шестнадцатиразрядный_регистр_3_out_4 , \шестнадцатиразрядный_регистр_4_out_4 ,
       \шестнадцатиразрядный_регистр_5_out_4 , \шестнадцатиразрядный_регистр_6_out_4 ,
       \шестнадцатиразрядный_регистр_7_out_4 , \шестнадцатиразрядный_регистр_8_out_4 ;

  Demultiplexer #(.select(3)) demultiplexer_1 (
    .out0(demultiplexer_1_out0), .out1(demultiplexer_1_out1), .out2(demultiplexer_1_out2),
    .out3(demultiplexer_1_out3), .out4(demultiplexer_1_out4), .out5(demultiplexer_1_out5),
    .out6(demultiplexer_1_out6), .out7(demultiplexer_1_out7), .in(in_1), .sel(in_3));  // open: en
  \шестнадцатиразрядный_регистр  \u_шестнадцатиразрядный_регистр_1  (
    .in_1(in_2), .in_2(demultiplexer_1_out0), .in_3(in_4), .out_4(\шестнадцатиразрядный_регистр_1_out_4 ));
  \шестнадцатиразрядный_регистр  \u_шестнадцатиразрядный_регистр_2  (
    .in_1(in_2), .in_2(demultiplexer_1_out1), .in_3(in_4), .out_4(\шестнадцатиразрядный_регистр_2_out_4 ));
  \шестнадцатиразрядный_регистр  \u_шестнадцатиразрядный_регистр_3  (
    .in_1(in_2), .in_2(demultiplexer_1_out2), .in_3(in_4), .out_4(\шестнадцатиразрядный_регистр_3_out_4 ));
  \шестнадцатиразрядный_регистр  \u_шестнадцатиразрядный_регистр_4  (
    .in_1(in_2), .in_2(demultiplexer_1_out3), .in_3(in_4), .out_4(\шестнадцатиразрядный_регистр_4_out_4 ));
  \шестнадцатиразрядный_регистр  \u_шестнадцатиразрядный_регистр_5  (
    .in_1(in_2), .in_2(demultiplexer_1_out4), .in_3(in_4), .out_4(\шестнадцатиразрядный_регистр_5_out_4 ));
  \шестнадцатиразрядный_регистр  \u_шестнадцатиразрядный_регистр_6  (
    .in_1(in_2), .in_2(demultiplexer_1_out5), .in_3(in_4), .out_4(\шестнадцатиразрядный_регистр_6_out_4 ));
  \шестнадцатиразрядный_регистр  \u_шестнадцатиразрядный_регистр_7  (
    .in_1(in_2), .in_2(demultiplexer_1_out6), .in_3(in_4), .out_4(\шестнадцатиразрядный_регистр_7_out_4 ));
  \шестнадцатиразрядный_регистр  \u_шестнадцатиразрядный_регистр_8  (
    .in_1(in_2), .in_2(demultiplexer_1_out7), .in_3(in_4), .out_4(\шестнадцатиразрядный_регистр_8_out_4 ));
  Multiplexer #(.select(3), .width(16)) multiplexer_1 (
    .in0(\шестнадцатиразрядный_регистр_1_out_4 ), .in1(\шестнадцатиразрядный_регистр_2_out_4 ),
    .in2(\шестнадцатиразрядный_регистр_3_out_4 ), .in3(\шестнадцатиразрядный_регистр_4_out_4 ),
    .in4(\шестнадцатиразрядный_регистр_5_out_4 ), .in5(\шестнадцатиразрядный_регистр_6_out_4 ),
    .in6(\шестнадцатиразрядный_регистр_7_out_4 ), .in7(\шестнадцатиразрядный_регистр_8_out_4 ), .out(out_5),
    .sel(in_3));  // open: en
endmodule
