// Logisim project Сумматор.circ as structural Verilog: 2 circuits, main circuit main
module main (
  input  A,
  input  in_2,
  input  in_3,
  input  in_4,
  input  in_5,
  input  in_6,
  input  in_7,
  input  B,
  input  in_9
);

  wire \сумматор_2_out_4 , \сумматор_3_out_4 , \сумматор_4_out_4 ;
  wire [3:0] \сумматор_4_out_5 ;

  Hex_Digit_Display hex_digit_display_1 (.value({A, in_2, in_3, in_4}));  // open: dp
  \Сумматор  \u_сумматор_1  (
    .in_1(A), .in_2(in_5), .in_3(\сумматор_2_out_4 ), .out_5(\сумматор_4_out_5 [3]));  // open: out_4
  \Сумматор  \u_сумматор_2  (
    .in_1(in_2), .in_2(in_6), .in_3(\сумматор_3_out_4 ), .out_4(\сумматор_2_out_4 ),
    .out_5(\сумматор_4_out_5 [2]));
  \Сумматор  \u_сумматор_3  (
    .in_1(in_3), .in_2(in_7), .in_3(\сумматор_4_out_4 ), .out_4(\сумматор_3_out_4 ),
    .out_5(\сумматор_4_out_5 [1]));
  Hex_Digit_Display hex_digit_display_2 (.value({in_5, in_6, in_7, B}));  // open: dp
  \Сумматор  \u_сумматор_4  (
    .in_1(in_4), .in_2(B), .in_3(in_9), .out_4(\сумматор_4_out_4 ), .out_5(\сумматор_4_out_5 [0]));
  Hex_Digit_Display hex_digit_display_3 (.value(\сумматор_4_out_5 ));  // open: dp

  // Notes on the sheet:
  //   +
  //   =
endmodule

module \Сумматор  (
  input  in_1,
  input  in_2,
  input  in_3,
  output out_4,
  output out_5
);

  wire and_1_out, and_2_out, and_3_out, xor_1_out;

  and and_1 (and_1_out, in_1, in_2);
  and and_2 (and_2_out, in_1, in_3);
  or or_1 (out_4, and_1_out, and_2_out, and_3_out);
  and and_3 (and_3_out, in_2, in_3);
  xor xor_1 (xor_1_out, in_2, in_3);
  xor xor_2 (out_5, in_1, xor_1_out);
endmodule
