// Logisim project Счетчик команд.circ as structural Verilog
// sum1
module \Сумматор  (
  input  in_1,
  input  in_2,
  input  in_3,
  output out_4,
  output out_5
);

  wire and_1_out, and_2_out, and_3_out, xor_1_out;

  and and_1 (and_1_out, in_1, in_2);
  and and_2 (and_2_out, in_1, in_3);
  and and_3 (and_3_out, in_2, in_3);
  or or_1 (out_4, and_1_out, and_2_out, and_3_out);
  xor xor_1 (xor_1_out, in_2, in_3);
  xor xor_2 (out_5, in_1, xor_1_out);
endmodule

// sum4
module \Сумматор_4bit  (
  input  [3:0] \Входы_B ,
  input  [3:0] \Входы_А ,
  input  in_3,
  output out_4,
  output [3:0] out_5
);

  wire \сумматор_2_out_4 , \сумматор_3_out_4 , \сумматор_4_out_4 ;

  \Сумматор  \u_сумматор_1  (
    .in_1(\Входы_А [3]), .in_2(\Входы_B [3]), .in_3(\сумматор_2_out_4 ), .out_4(out_4), .out_5(out_5[3]));
  \Сумматор  \u_сумматор_2  (
    .in_1(\Входы_А [2]), .in_2(\Входы_B [2]), .in_3(\сумматор_3_out_4 ), .out_4(\сумматор_2_out_4 ),
    .out_5(out_5[2]));
  \Сумматор  \u_сумматор_3  (
    .in_1(\Входы_А [1]), .in_2(\Входы_B [1]), .in_3(\сумматор_4_out_4 ), .out_4(\сумматор_3_out_4 ),
    .out_5(out_5[1]));
  \Сумматор  \u_сумматор_4  (
    .in_1(\Входы_А [0]), .in_2(\Входы_B [0]), .in_3(in_3), .out_4(\сумматор_4_out_4 ), .out_5(out_5[0]));
endmodule

// Add1
module \Сумматор_16bit  (
  input  [15:0] in_1,
  input  in_2,
  output [15:0] out_3
);

  wire \сумматор_4bit_2_out_4 , \сумматор_4bit_3_out_4 , \сумматор_4bit_4_out_4 ;

  \Сумматор_4bit  \u_сумматор_4bit_1  (
    .\Входы_А (in_1[15:12]), .\Входы_B (4'b0000), .out_5(out_3[15:12]), .in_3(\сумматор_4bit_2_out_4 ));  // open: out_4
  \Сумматор_4bit  \u_сумматор_4bit_2  (
    .out_4(\сумматор_4bit_2_out_4 ), .\Входы_А (in_1[11:8]), .\Входы_B (4'b0000), .out_5(out_3[11:8]),
    .in_3(\сумматор_4bit_3_out_4 ));
  \Сумматор_4bit  \u_сумматор_4bit_3  (
    .out_4(\сумматор_4bit_3_out_4 ), .\Входы_А (in_1[7:4]), .\Входы_B (4'b0000), .out_5(out_3[7:4]),
    .in_3(\сумматор_4bit_4_out_4 ));
  \Сумматор_4bit  \u_сумматор_4bit_4  (
    .out_4(\сумматор_4bit_4_out_4 ), .\Входы_А (in_1[3:0]), .\Входы_B (4'b0000), .out_5(out_3[3:0]),
    .in_3(in_2));
endmodule

module \Счетчик_команд  (
  input  in_1,
  input  \ввод_данных ,
  input  \сброс ,
  input  [15:0] in_4,
  input  \тактовый ,
  output [15:0] out_6,
  output [15:0] out_7
);

  wire or_1_out;
  wire [15:0] multiplexer_1_out, multiplexer_2_out;

  Multiplexer #(.width(16)) multiplexer_1 (
    .in0(in_4), .in1({16{1'b0}}), .out(multiplexer_1_out), .sel(\сброс ));  // open: en
  or or_1 (or_1_out, \ввод_данных , \сброс );
  Multiplexer #(.width(16)) multiplexer_2 (
    .in0(out_7), .in1(multiplexer_1_out), .out(multiplexer_2_out), .sel(or_1_out));  // open: en
  \шестнадцатиразрядный_регистр  \u_шестнадцатиразрядный_регистр_1  (
    .in_1(multiplexer_2_out), .in_2(1'b1), .in_3(\тактовый ), .out_4(out_6));
  \Сумматор_16bit  \u_сумматор_16bit_1  (.in_1(out_6), .out_3(out_7), .in_2(in_1));

  // Notes on the sheet:
  //   Счетчик
endmodule
