// Logisim project Триггеры.circ as structural Verilog
module \RS_триггер  (
  input  S,
  input  R,
  output minus_Q,
  output Q
);

  nor nor_1 (minus_Q, S, Q);
  nor nor_2 (Q, minus_Q, R);
endmodule

module \RS_Триггер_2  (
  input  in_1,
  input  in_2
);

  wire s_r_ff_1_q, s_r_ff_1_qn;

  S_R_Flip_Flop #(.trigger("low")) s_r_ff_1 (
    .S(in_1), .clk(1'b0), .R(in_2), .Q(s_r_ff_1_q), .Qn(s_r_ff_1_qn));  // open: preset, reset, en
  LED led_1 (.in(s_r_ff_1_q));
  LED led_2 (.in(s_r_ff_1_qn));
endmodule

module \JK_триггера  (
  input  in_1,
  input  in_2,
  input  in_3
);

  wire j_k_ff_1_q, j_k_ff_1_qn;

  LED led_1 (.in(j_k_ff_1_q));
  J_K_Flip_Flop #(.trigger("falling")) j_k_ff_1 (
    .J(in_1), .clk(in_2), .K(in_3), .Q(j_k_ff_1_q), .Qn(j_k_ff_1_qn));  // open: preset, en, reset
  LED led_2 (.in(j_k_ff_1_qn));
endmodule
